# Fritzing sketch pulsepcb (saved by Fritzing 0.9.3b)
circuit board: 7.62cm x 15.24cm
breadboards: 1

parts:
  S4 = Momentary Switch [package=ksa_sealed_tac_switch]
  Part1 = Adafruit Metro Mini [part_number="Adafruit #2590"]
  S5 = Momentary Switch [package=ksa_sealed_tac_switch]
  S6 = Momentary Switch [package=ksa_sealed_tac_switch]
  S7 = Momentary Switch [package=ksa_sealed_tac_switch]
  R7 = TRIMPOT [package=trimpot_pth_s3_lock]
  U2 = 74HC595 [package="DIP16 [THT]"]
  U3 = 74HC595 [package="DIP16 [THT]"]
  R8 = Resistor [tolerance=±5% resistance=470 package=THT]
  LED1 = smd LED [color="Red (633nm)" package="0603 [SMD]"]
  R9 = Resistor [tolerance=±5% resistance=470 package=THT]
  LED2 = smd LED [color="Red (633nm)" package="0603 [SMD]"]
  R10 = Resistor [tolerance=±5% resistance=470 package=THT]
  LED3 = smd LED [color="Red (633nm)" package="0603 [SMD]"]
  R11 = Resistor [tolerance=±5% resistance=470 package=THT]
  LED4 = smd LED [color="Red (633nm)" package="0603 [SMD]"]
  R12 = Resistor [tolerance=±5% resistance=470 package=THT]
  LED5 = smd LED [color="Red (633nm)" package="0603 [SMD]"]
  R13 = Resistor [tolerance=±5% resistance=470 package=THT]
  LED6 = smd LED [color="Red (633nm)" package="0603 [SMD]"]
  R14 = Resistor [tolerance=±5% resistance=470 package=THT]
  LED7 = smd LED [color="Red (633nm)" package="0603 [SMD]"]
  R15 = Resistor [tolerance=±5% resistance=470 package=THT]
  LED8 = smd LED [color="Red (633nm)" package="0603 [SMD]"]
  R16 = Resistor [tolerance=±5% resistance=470 package=THT]
  LED9 = smd LED [color="Red (633nm)" package="0603 [SMD]"]
  R17 = Resistor [tolerance=±5% resistance=470 package=THT]
  LED10 = smd LED [color="Red (633nm)" package="0603 [SMD]"]
  R18 = Resistor [tolerance=±5% resistance=470 package=THT]
  LED11 = smd LED [color="Red (633nm)" package="0603 [SMD]"]
  R19 = Resistor [tolerance=±5% resistance=470 package=THT]
  LED12 = smd LED [color="Red (633nm)" package="0603 [SMD]"]
  R20 = Resistor [tolerance=±5% resistance=470 package=THT]
  LED13 = smd LED [color="Red (633nm)" package="0603 [SMD]"]
  R21 = Resistor [tolerance=±5% resistance=470 package=THT]
  LED14 = smd LED [color="Red (633nm)" package="0603 [SMD]"]
  R22 = Resistor [tolerance=±5% resistance=470 package=THT]
  LED15 = smd LED [color="Red (633nm)" package="0603 [SMD]"]
  R23 = Resistor [tolerance=±5% resistance=470 package=THT]
  LED16 = smd LED [color="Red (633nm)" package="0603 [SMD]"]
  R24 = Resistor [tolerance=±5% resistance=470 package=THT]
  LED17 = smd LED [color="Red (633nm)" package="0603 [SMD]"]
  R25 = Resistor [tolerance=±5% resistance=470 package=THT]
  LED18 = smd LED [color="Red (633nm)" package="0603 [SMD]"]
  R26 = Resistor [tolerance=±5% resistance=470 package=THT]
  LED19 = smd LED [color="Red (633nm)" package="0603 [SMD]"]
  R27 = Resistor [tolerance=±5% resistance=470 package=THT]
  LED20 = smd LED [color="Red (633nm)" package="0603 [SMD]"]

nets:
  GND: S4.1, Part1.GND, S5.1, S6.1, S7.1, R7.CW, U2.GND, U2.OE, U3.GND, U3.OE, LED1.cathode, LED2.cathode, LED3.cathode, LED4.cathode, LED5.cathode, LED6.cathode, LED7.cathode, LED8.cathode, LED9.cathode, LED10.cathode, LED11.cathode, LED12.cathode, LED13.cathode, LED14.cathode, LED15.cathode, LED16.cathode, LED17.cathode, LED18.cathode, LED19.cathode, LED20.cathode
  N1: S4.2, Part1.IO2
  VCC: S4.3, Part1.+5V, S5.3, S6.3, S7.3, R7.CCW, U2.MR, U2.VCC, U3.MR, U3.VCC
  N2: Part1.AD0, R7.WIPER
  N3: Part1.IO13, U2.SH_CP
  N4: Part1.IO12, U2.ST_CP
  N5: Part1.IO11, U2.DS
  N6: Part1.IO10, R27.Pin_1
  N7: Part1.IO9, R26.Pin_1
  N8: Part1.IO8, R25.Pin_1
  N9: Part1.IO7, R24.Pin_1
  N10: Part1.IO5, S7.2
  N11: Part1.IO4, S6.2
  N12: Part1.IO3, S5.2
  N13: U2.Q1, R9.Pin_1
  N14: U2.Q2, R10.Pin_1
  N15: U2.Q3, R11.Pin_1
  N16: U2.Q4, R12.Pin_1
  N17: U2.Q5, R13.Pin_1
  N18: U2.Q6, R14.Pin_1
  N19: U2.Q7, R15.Pin_1
  N20: U2.Q7', U3.DS
  N21: U2.Q0, R8.Pin_1
  N22: U3.Q1, R17.Pin_1
  N23: U3.Q2, R18.Pin_1
  N24: U3.Q3, R19.Pin_1
  N25: U3.Q4, R20.Pin_1
  N26: U3.Q5, R21.Pin_1
  N27: U3.Q6, R22.Pin_1
  N28: U3.Q7, R23.Pin_1
  N29: U3.Q0, R16.Pin_1
  N30: R8.Pin_0, LED1.anode
  N31: R9.Pin_0, LED2.anode
  N32: R10.Pin_0, LED3.anode
  N33: R11.Pin_0, LED4.anode
  N34: R12.Pin_0, LED5.anode
  N35: R13.Pin_0, LED6.anode
  N36: R14.Pin_0, LED7.anode
  N37: R15.Pin_0, LED8.anode
  N38: R16.Pin_0, LED9.anode
  N39: R17.Pin_0, LED10.anode
  N40: R18.Pin_0, LED11.anode
  N41: R19.Pin_0, LED12.anode
  N42: R20.Pin_0, LED13.anode
  N43: R21.Pin_0, LED14.anode
  N44: R22.Pin_0, LED15.anode
  N45: R23.Pin_0, LED16.anode
  N46: R24.Pin_0, LED17.anode
  N47: R25.Pin_0, LED18.anode
  N48: R26.Pin_0, LED19.anode
  N49: R27.Pin_0, LED20.anode

custom parts:
  Adafruit Metro Mini: We sure love the ATmega328 here at Adafruit, and we use them a lot for our own projects. The processor has plenty of GPIO, Analog inputs, hardware UART SPI and I2C, timers and PWM galore - just enough for most simple projects. When we need to go small, we use a Pro Trinket 3V or 5V, but if you want to have USB-to-Serial built in, we reach for an Adafruit METRO Mini. METRO Mini is the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
